# Fritzing sketch VJAS_Schematic (saved by Fritzing 0.9.0b)
breadboards: 1

parts:
  IC1 = H-Bridge [package=THT]
  L1 = Solenoid
  Part1 = Arduino Uno (Rev3)
  VCC1 = Battery block 9V

nets:
  N1: IC1.1_2EN, Part1.D9_PWM
  N2: IC1.1A, Part1.D3_PWM
  N3: IC1.1Y, L1.pin2
  GND1: IC1.GND1, IC1.GND2, Part1.GND, VCC1.-
  N4: IC1.2Y, L1.pin1
  N5: IC1.2A, Part1.D2
  N6: IC1.VCC2, VCC1.+
  N7: IC1.3_4EN, IC1.VCC1, Part1.5V
